# Fritzing sketch FT-817 Teensy-3.2 (saved by Fritzing 0.9.3b)
circuit board: 23.3123cm x 11.4032cm

parts:
  Teensy_3_2 = Teensy 3.1
  R1 = Resistor [tolerance=±5% resistance=180k package=THT]
  D1 = Rectifier Diode [part_number=1N4001 package="300 mil [THT]"]
  C1 = Capacitor [part_number=10nf package=cap-pth-small2]
  R2 = Resistor [tolerance=±5% resistance=5.6k package=THT]
  C2 = Capacitor [part_number=10nf package=cap-pth-small2]
  R3 = Resistor [tolerance=±5% resistance=38k package=THT]

nets:
  0V: Teensy_3_2.GND, R1.Pin_0, R2.Pin_1
  N1: Teensy_3_2.D0, R1.Pin_1, R3.Pin_1
  N2: Teensy_3_2.A14/DAC, C1.1
  N3: Teensy_3_2.A2/D16, C2.1
  N4: Teensy_3_2.Vin, D1.cathode
  9.6V: D1.anode
  Audio OUT: C1.2
  Audio IN: C2.2
  Filter Select: R3.Pin_0
