# Fritzing sketch Inline Audio DSP Teensy-3.2 (saved by Fritzing 0.9.3b)
circuit board: 23.3123cm x 11.4032cm

parts:
  Teensy_3_2 = Teensy 3.1
  C1 = Capacitor [part_number=10nf package=cap-pth-small2]
  R2 = Resistor [tolerance=±5% resistance=47 package=THT]
  C2 = Capacitor [part_number=10nf package=cap-pth-small2]
  U2 = 3.5mm Audio Jack [part_number="Audio Out" package=audio-jack-3.5mm-smd]
  U3 = 3.5mm Audio Jack [package=audio-jack-3.5mm-smd]

nets:
  N1: Teensy_3_2.GND, R2.Pin_1, U2.SLEEVE, U3.SLEEVE
  N2: Teensy_3_2.A14/DAC, C1.1
  N3: Teensy_3_2.A2/D16, R2.Pin_0, C2.1
  N4: C1.2, U2.RIGHT, U2.LEFT
  N5: C2.2, U3.RIGHT, U3.LEFT
